# Fritzing sketch Arduino_binary_buttons (saved by Fritzing 0.9.3b)
breadboards: 2

parts:
  S2 = Momentary Switch [package=ksa_sealed_tac_switch]
  S3 = Momentary Switch [package=ksa_sealed_tac_switch]
  S4 = Momentary Switch [package=ksa_sealed_tac_switch]
  S5 = Momentary Switch [package=ksa_sealed_tac_switch]
  S6 = Momentary Switch [package=ksa_sealed_tac_switch]
  S7 = Momentary Switch [package=ksa_sealed_tac_switch]
  S8 = Momentary Switch [package=ksa_sealed_tac_switch]
  part = Arduino Pro Mini v13
  part_2 = P1000K
  part_3 = P1000K
  part_4 = P1000K
  part_5 = P1000K
  part_6 = P1000K
  part_7 = P1000K
  part_8 = P1000K
  part_9 = P1000K
  part_10 = P1000K

nets:
  N1: S2.2, S3.2, S4.2, S5.2, S6.2, S7.2, S8.2, part.GND
  N2: S2.3, part.D2, part_2.anode, part_8.anode, part_10.anode
  N3: S3.3, part.D3_PWM, part_3.anode, part_5.anode, part_9.anode
  N4: S4.3, part_8.cathode, part_9.cathode
  N5: S5.3, part.D4, part_4.anode, part_6.anode, part_7.anode
  N6: S6.3, part_7.cathode, part_10.cathode
  N7: S7.3, part_5.cathode, part_6.cathode
  N8: S8.3, part_2.cathode, part_3.cathode, part_4.cathode
